// Digital circuit Ejercicio2.dig as structural Verilog
module Ejercicio2 (
  input  [63:0] data,
  input  [3:0] limit,
  output [31:0] crc
);

  wire comparator_1_gt, comparator_2_gt, comparator_3_gt, comparator_4_gt, comparator_5_gt, comparator_6_gt,
       comparator_7_gt, comparator_8_gt;
  wire [7:0] multiplexer_2_out, multiplexer_5_out, multiplexer_5_out_2, multiplexer_5_out_3, xor_1_out,
       xor_3_out, xor_5_out, xor_7_out, xor_9_out, xor_11_out, xor_13_out, xor_15_out;
  wire [31:0] multiplexer_4_out, multiplexer_6_out, multiplexer_7_out, Table_2_d, Table_3_d, Table_4_d,
       Table_5_d, Table_6_d, Table_7_d, Table_8_d, Table_d, xor_2_out, xor_4_out, xor_6_out, xor_8_out,
       xor_10_out, xor_12_out, xor_14_out, xor_16_out;
  wire [31:8] multiplexer_1_out, multiplexer_2_out_2, multiplexer_3_out;
  wire [31:24] multiplexer_1_out_2, multiplexer_3_out_2, multiplexer_5_out_4;

  Comparator #(.Bits(4)) comparator_1 (.a(limit), .b(4'b0000), .gt(comparator_1_gt));  // open: eq, lt
  assign xor_1_out = {8{1'b0}} ^ data[7:0];  // XOr xor_1, 8 bits wide
  ROM #(.AddrBits(8), .Bits(32)) Table (.A(xor_1_out), .sel(1'b1), .D(Table_d));
  assign xor_2_out = {32{1'b0}} ^ Table_d;  // XOr xor_2, 32 bits wide
  Multiplexer #(.Bits(32)) multiplexer_1 (
    .sel(comparator_1_gt), .in_0({32{1'b0}}), .in_1(xor_2_out), .out({multiplexer_1_out_2, multiplexer_1_out}));
  Comparator #(.Bits(4)) comparator_2 (.a(limit), .b(4'b0001), .gt(comparator_2_gt));  // open: eq, lt
  assign xor_3_out = multiplexer_1_out[15:8] ^ data[15:8];  // XOr xor_3, 8 bits wide
  ROM #(.AddrBits(8), .Bits(32)) Table_2 (.A(xor_3_out), .sel(1'b1), .D(Table_2_d));
  assign xor_4_out = {multiplexer_1_out, {8{1'b0}}} ^ Table_2_d;  // XOr xor_4, 32 bits wide
  Multiplexer #(.Bits(32)) multiplexer_2 (
    .sel(comparator_2_gt), .in_0({multiplexer_1_out_2, multiplexer_1_out}), .in_1(xor_4_out),
    .out({multiplexer_2_out_2, multiplexer_2_out}));
  Comparator #(.Bits(4)) comparator_3 (.a(limit), .b(4'b0010), .gt(comparator_3_gt));  // open: eq, lt
  assign xor_5_out = multiplexer_2_out ^ data[23:16];  // XOr xor_5, 8 bits wide
  ROM #(.AddrBits(8), .Bits(32)) Table_3 (.A(xor_5_out), .sel(1'b1), .D(Table_3_d));
  assign xor_6_out = {multiplexer_2_out_2[23:8], multiplexer_2_out, {8{1'b0}}} ^ Table_3_d;  // XOr xor_6, 32 bits wide
  Multiplexer #(.Bits(32)) multiplexer_3 (
    .sel(comparator_3_gt), .in_0({multiplexer_2_out_2, multiplexer_2_out}), .in_1(xor_6_out),
    .out({multiplexer_3_out_2, multiplexer_3_out}));
  Comparator #(.Bits(4)) comparator_4 (.a(limit), .b(4'b0011), .gt(comparator_4_gt));  // open: eq, lt
  assign xor_7_out = multiplexer_3_out[15:8] ^ data[31:24];  // XOr xor_7, 8 bits wide
  ROM #(.AddrBits(8), .Bits(32)) Table_4 (.A(xor_7_out), .sel(1'b1), .D(Table_4_d));
  assign xor_8_out = {multiplexer_3_out, {8{1'b0}}} ^ Table_4_d;  // XOr xor_8, 32 bits wide
  Multiplexer #(.Bits(32)) multiplexer_4 (
    .sel(comparator_4_gt), .in_0({multiplexer_3_out_2, multiplexer_3_out}), .in_1(xor_8_out),
    .out(multiplexer_4_out));
  Comparator #(.Bits(4)) comparator_5 (.a(limit), .b(4'b0100), .gt(comparator_5_gt));  // open: eq, lt
  assign xor_9_out = multiplexer_4_out[7:0] ^ data[39:32];  // XOr xor_9, 8 bits wide
  ROM #(.AddrBits(8), .Bits(32)) Table_5 (.A(xor_9_out), .sel(1'b1), .D(Table_5_d));
  assign xor_10_out = {multiplexer_4_out[23:0], {8{1'b0}}} ^ Table_5_d;  // XOr xor_10, 32 bits wide
  Multiplexer #(.Bits(32)) multiplexer_5 (
    .sel(comparator_5_gt), .in_0(multiplexer_4_out), .in_1(xor_10_out),
    .out({multiplexer_5_out_4, multiplexer_5_out_3, multiplexer_5_out_2, multiplexer_5_out}));
  Comparator #(.Bits(4)) comparator_6 (.a(limit), .b(4'b0101), .gt(comparator_6_gt));  // open: eq, lt
  assign xor_11_out = multiplexer_5_out ^ data[47:40];  // XOr xor_11, 8 bits wide
  ROM #(.AddrBits(8), .Bits(32)) Table_6 (.A(xor_11_out), .sel(1'b1), .D(Table_6_d));
  assign xor_12_out = {multiplexer_5_out_3, multiplexer_5_out_2, multiplexer_5_out, {8{1'b0}}} ^ Table_6_d;  // XOr xor_12, 32 bits wide
  Multiplexer #(.Bits(32)) multiplexer_6 (
    .sel(comparator_6_gt),
    .in_0({multiplexer_5_out_4, multiplexer_5_out_3, multiplexer_5_out_2, multiplexer_5_out}),
    .in_1(xor_12_out), .out(multiplexer_6_out));
  Comparator #(.Bits(4)) comparator_7 (.a(limit), .b(4'b0110), .gt(comparator_7_gt));  // open: eq, lt
  assign xor_13_out = multiplexer_6_out[7:0] ^ data[55:48];  // XOr xor_13, 8 bits wide
  ROM #(.AddrBits(8), .Bits(32)) Table_7 (.A(xor_13_out), .sel(1'b1), .D(Table_7_d));
  assign xor_14_out = {multiplexer_6_out[23:0], {8{1'b0}}} ^ Table_7_d;  // XOr xor_14, 32 bits wide
  Multiplexer #(.Bits(32)) multiplexer_7 (
    .sel(comparator_7_gt), .in_0(multiplexer_6_out), .in_1(xor_14_out), .out(multiplexer_7_out));
  assign xor_15_out = multiplexer_7_out[7:0] ^ data[63:56];  // XOr xor_15, 8 bits wide
  Comparator #(.Bits(4)) comparator_8 (.a(limit), .b(4'b0111), .gt(comparator_8_gt));  // open: eq, lt
  ROM #(.AddrBits(8), .Bits(32)) Table_8 (.A(xor_15_out), .sel(1'b1), .D(Table_8_d));
  assign xor_16_out = {multiplexer_7_out[23:0], {8{1'b0}}} ^ Table_8_d;  // XOr xor_16, 32 bits wide
  Multiplexer #(.Bits(32)) multiplexer_8 (
    .sel(comparator_8_gt), .in_0(multiplexer_7_out), .in_1(xor_16_out), .out(crc));

  // Notes on the sheet:
  //   contents of Table (hex, n*v repeats v):
  //   d202ef8d,a505df1b,3c0c8ea1,4b0bbe37,d56f2b94,a2681b02,3b614ab8,4c667a2e,dcd967bf,
  //   abde5729,32d70693,45d03605,dbb4a3a6,acb39330,35bac28a,42bdf21c,cfb5ffe9,b8b2cf7f,
  //   21bb9ec5,56bcae53,c8d83bf0,bfdf0b66,26d65adc,51d16a4a,c16e77db,b669474d,2f6016f7,
  //   58672661,c603b3c2,b1048354,280dd2ee,5f0ae278,e96ccf45,9e6bffd3,762ae69,70659eff,ee010b5c,
  //   99063bca,f6a70,77085ae6,e7b74777,90b077e1,9b9265b,7ebe16cd,e0da836e,97ddb3f8,ed4e242,
  //   79d3d2d4,f4dbdf21,83dcefb7,1ad5be0d,6dd28e9b,f3b61b38,84b12bae,1db87a14,6abf4a82,
  //   fa005713,8d076785,140e363f,630906a9,fd6d930a,8a6aa39c,1363f226,6464c2b0,a4deae1d,
  //   d3d99e8b,4ad0cf31,3dd7ffa7,a3b36a04,d4b45a92,4dbd0b28,3aba3bbe,aa05262f,dd0216b9,
  //   440b4703,330c7795,ad68e236,da6fd2a0,4366831a,3461b38c,b969be79,ce6e8eef,5767df55,
  //   2060efc3,be047a60,c9034af6,500a1b4c,270d2bda,b7b2364b,c0b506dd,59bc5767,2ebb67f1,
  //   b0dff252,c7d8c2c4,5ed1937e,29d6a3e8,9fb08ed5,e8b7be43,71beeff9,6b9df6f,98dd4acc,efda7a5a,
  //   76d32be0,1d41b76,916b06e7,e66c3671,7f6567cb,862575d,9606c2fe,e101f268,7808a3d2,f0f9344,
  //   82079eb1,f500ae27,6c09ff9d,1b0ecf0b,856a5aa8,f26d6a3e,6b643b84,1c630b12,8cdc1683,
  //   fbdb2615,62d277af,15d54739,8bb1d29a,fcb6e20c,65bfb3b6,12b88320,3fba6cad,48bd5c3b,
  //   d1b40d81,a6b33d17,38d7a8b4,4fd09822,d6d9c998,a1def90e,3161e49f,4666d409,df6f85b3,
  //   a868b525,360c2086,410b1010,d80241aa,af05713c,220d7cc9,550a4c5f,cc031de5,bb042d73,
  //   2560b8d0,52678846,cb6ed9fc,bc69e96a,2cd6f4fb,5bd1c46d,c2d895d7,b5dfa541,2bbb30e2,
  //   5cbc0074,c5b551ce,b2b26158,4d44c65,73d37cf3,eada2d49,9ddd1ddf,3b9887c,74beb8ea,edb7e950,
  //   9ab0d9c6,a0fc457,7d08f4c1,e401a57b,930695ed,d62004e,7a6530d8,e36c6162,946b51f4,19635c01,
  //   6e646c97,f76d3d2d,806a0dbb,1e0e9818,6909a88e,f000f934,8707c9a2,17b8d433,60bfe4a5,
  //   f9b6b51f,8eb18589,10d5102a,67d220bc,fedb7106,89dc4190,49662d3d,3e611dab,a7684c11,
  //   d06f7c87,4e0be924,390cd9b2,a0058808,d702b89e,47bda50f,30ba9599,a9b3c423,deb4f4b5,
  //   40d06116,37d75180,aede003a,d9d930ac,54d13d59,23d60dcf,badf5c75,cdd86ce3,53bcf940,
  //   24bbc9d6,bdb2986c,cab5a8fa,5a0ab56b,2d0d85fd,b404d447,c303e4d1,5d677172,2a6041e4,
  //   b369105e,c46e20c8,72080df5,50f3d63,9c066cd9,eb015c4f,7565c9ec,262f97a,9b6ba8c0,ec6c9856,
  //   7cd385c7,bd4b551,92dde4eb,e5dad47d,7bbe41de,cb97148,95b020f2,e2b71064,6fbf1d91,18b82d07,
  //   81b17cbd,f6b64c2b,68d2d988,1fd5e91e,86dcb8a4,f1db8832,616495a3,1663a535,8f6af48f,
  //   f86dc419,660951ba,110e612c,88073096,ff000000
  //   contents of Table_2 (hex, n*v repeats v):
  //   d202ef8d,a505df1b,3c0c8ea1,4b0bbe37,d56f2b94,a2681b02,3b614ab8,4c667a2e,dcd967bf,
  //   abde5729,32d70693,45d03605,dbb4a3a6,acb39330,35bac28a,42bdf21c,cfb5ffe9,b8b2cf7f,
  //   21bb9ec5,56bcae53,c8d83bf0,bfdf0b66,26d65adc,51d16a4a,c16e77db,b669474d,2f6016f7,
  //   58672661,c603b3c2,b1048354,280dd2ee,5f0ae278,e96ccf45,9e6bffd3,762ae69,70659eff,ee010b5c,
  //   99063bca,f6a70,77085ae6,e7b74777,90b077e1,9b9265b,7ebe16cd,e0da836e,97ddb3f8,ed4e242,
  //   79d3d2d4,f4dbdf21,83dcefb7,1ad5be0d,6dd28e9b,f3b61b38,84b12bae,1db87a14,6abf4a82,
  //   fa005713,8d076785,140e363f,630906a9,fd6d930a,8a6aa39c,1363f226,6464c2b0,a4deae1d,
  //   d3d99e8b,4ad0cf31,3dd7ffa7,a3b36a04,d4b45a92,4dbd0b28,3aba3bbe,aa05262f,dd0216b9,
  //   440b4703,330c7795,ad68e236,da6fd2a0,4366831a,3461b38c,b969be79,ce6e8eef,5767df55,
  //   2060efc3,be047a60,c9034af6,500a1b4c,270d2bda,b7b2364b,c0b506dd,59bc5767,2ebb67f1,
  //   b0dff252,c7d8c2c4,5ed1937e,29d6a3e8,9fb08ed5,e8b7be43,71beeff9,6b9df6f,98dd4acc,efda7a5a,
  //   76d32be0,1d41b76,916b06e7,e66c3671,7f6567cb,862575d,9606c2fe,e101f268,7808a3d2,f0f9344,
  //   82079eb1,f500ae27,6c09ff9d,1b0ecf0b,856a5aa8,f26d6a3e,6b643b84,1c630b12,8cdc1683,
  //   fbdb2615,62d277af,15d54739,8bb1d29a,fcb6e20c,65bfb3b6,12b88320,3fba6cad,48bd5c3b,
  //   d1b40d81,a6b33d17,38d7a8b4,4fd09822,d6d9c998,a1def90e,3161e49f,4666d409,df6f85b3,
  //   a868b525,360c2086,410b1010,d80241aa,af05713c,220d7cc9,550a4c5f,cc031de5,bb042d73,
  //   2560b8d0,52678846,cb6ed9fc,bc69e96a,2cd6f4fb,5bd1c46d,c2d895d7,b5dfa541,2bbb30e2,
  //   5cbc0074,c5b551ce,b2b26158,4d44c65,73d37cf3,eada2d49,9ddd1ddf,3b9887c,74beb8ea,edb7e950,
  //   9ab0d9c6,a0fc457,7d08f4c1,e401a57b,930695ed,d62004e,7a6530d8,e36c6162,946b51f4,19635c01,
  //   6e646c97,f76d3d2d,806a0dbb,1e0e9818,6909a88e,f000f934,8707c9a2,17b8d433,60bfe4a5,
  //   f9b6b51f,8eb18589,10d5102a,67d220bc,fedb7106,89dc4190,49662d3d,3e611dab,a7684c11,
  //   d06f7c87,4e0be924,390cd9b2,a0058808,d702b89e,47bda50f,30ba9599,a9b3c423,deb4f4b5,
  //   40d06116,37d75180,aede003a,d9d930ac,54d13d59,23d60dcf,badf5c75,cdd86ce3,53bcf940,
  //   24bbc9d6,bdb2986c,cab5a8fa,5a0ab56b,2d0d85fd,b404d447,c303e4d1,5d677172,2a6041e4,
  //   b369105e,c46e20c8,72080df5,50f3d63,9c066cd9,eb015c4f,7565c9ec,262f97a,9b6ba8c0,ec6c9856,
  //   7cd385c7,bd4b551,92dde4eb,e5dad47d,7bbe41de,cb97148,95b020f2,e2b71064,6fbf1d91,18b82d07,
  //   81b17cbd,f6b64c2b,68d2d988,1fd5e91e,86dcb8a4,f1db8832,616495a3,1663a535,8f6af48f,
  //   f86dc419,660951ba,110e612c,88073096,ff000000
  //   contents of Table_3 (hex, n*v repeats v):
  //   d202ef8d,a505df1b,3c0c8ea1,4b0bbe37,d56f2b94,a2681b02,3b614ab8,4c667a2e,dcd967bf,
  //   abde5729,32d70693,45d03605,dbb4a3a6,acb39330,35bac28a,42bdf21c,cfb5ffe9,b8b2cf7f,
  //   21bb9ec5,56bcae53,c8d83bf0,bfdf0b66,26d65adc,51d16a4a,c16e77db,b669474d,2f6016f7,
  //   58672661,c603b3c2,b1048354,280dd2ee,5f0ae278,e96ccf45,9e6bffd3,762ae69,70659eff,ee010b5c,
  //   99063bca,f6a70,77085ae6,e7b74777,90b077e1,9b9265b,7ebe16cd,e0da836e,97ddb3f8,ed4e242,
  //   79d3d2d4,f4dbdf21,83dcefb7,1ad5be0d,6dd28e9b,f3b61b38,84b12bae,1db87a14,6abf4a82,
  //   fa005713,8d076785,140e363f,630906a9,fd6d930a,8a6aa39c,1363f226,6464c2b0,a4deae1d,
  //   d3d99e8b,4ad0cf31,3dd7ffa7,a3b36a04,d4b45a92,4dbd0b28,3aba3bbe,aa05262f,dd0216b9,
  //   440b4703,330c7795,ad68e236,da6fd2a0,4366831a,3461b38c,b969be79,ce6e8eef,5767df55,
  //   2060efc3,be047a60,c9034af6,500a1b4c,270d2bda,b7b2364b,c0b506dd,59bc5767,2ebb67f1,
  //   b0dff252,c7d8c2c4,5ed1937e,29d6a3e8,9fb08ed5,e8b7be43,71beeff9,6b9df6f,98dd4acc,efda7a5a,
  //   76d32be0,1d41b76,916b06e7,e66c3671,7f6567cb,862575d,9606c2fe,e101f268,7808a3d2,f0f9344,
  //   82079eb1,f500ae27,6c09ff9d,1b0ecf0b,856a5aa8,f26d6a3e,6b643b84,1c630b12,8cdc1683,
  //   fbdb2615,62d277af,15d54739,8bb1d29a,fcb6e20c,65bfb3b6,12b88320,3fba6cad,48bd5c3b,
  //   d1b40d81,a6b33d17,38d7a8b4,4fd09822,d6d9c998,a1def90e,3161e49f,4666d409,df6f85b3,
  //   a868b525,360c2086,410b1010,d80241aa,af05713c,220d7cc9,550a4c5f,cc031de5,bb042d73,
  //   2560b8d0,52678846,cb6ed9fc,bc69e96a,2cd6f4fb,5bd1c46d,c2d895d7,b5dfa541,2bbb30e2,
  //   5cbc0074,c5b551ce,b2b26158,4d44c65,73d37cf3,eada2d49,9ddd1ddf,3b9887c,74beb8ea,edb7e950,
  //   9ab0d9c6,a0fc457,7d08f4c1,e401a57b,930695ed,d62004e,7a6530d8,e36c6162,946b51f4,19635c01,
  //   6e646c97,f76d3d2d,806a0dbb,1e0e9818,6909a88e,f000f934,8707c9a2,17b8d433,60bfe4a5,
  //   f9b6b51f,8eb18589,10d5102a,67d220bc,fedb7106,89dc4190,49662d3d,3e611dab,a7684c11,
  //   d06f7c87,4e0be924,390cd9b2,a0058808,d702b89e,47bda50f,30ba9599,a9b3c423,deb4f4b5,
  //   40d06116,37d75180,aede003a,d9d930ac,54d13d59,23d60dcf,badf5c75,cdd86ce3,53bcf940,
  //   24bbc9d6,bdb2986c,cab5a8fa,5a0ab56b,2d0d85fd,b404d447,c303e4d1,5d677172,2a6041e4,
  //   b369105e,c46e20c8,72080df5,50f3d63,9c066cd9,eb015c4f,7565c9ec,262f97a,9b6ba8c0,ec6c9856,
  //   7cd385c7,bd4b551,92dde4eb,e5dad47d,7bbe41de,cb97148,95b020f2,e2b71064,6fbf1d91,18b82d07,
  //   81b17cbd,f6b64c2b,68d2d988,1fd5e91e,86dcb8a4,f1db8832,616495a3,1663a535,8f6af48f,
  //   f86dc419,660951ba,110e612c,88073096,ff000000
  //   contents of Table_4 (hex, n*v repeats v):
  //   d202ef8d,a505df1b,3c0c8ea1,4b0bbe37,d56f2b94,a2681b02,3b614ab8,4c667a2e,dcd967bf,
  //   abde5729,32d70693,45d03605,dbb4a3a6,acb39330,35bac28a,42bdf21c,cfb5ffe9,b8b2cf7f,
  //   21bb9ec5,56bcae53,c8d83bf0,bfdf0b66,26d65adc,51d16a4a,c16e77db,b669474d,2f6016f7,
  //   58672661,c603b3c2,b1048354,280dd2ee,5f0ae278,e96ccf45,9e6bffd3,762ae69,70659eff,ee010b5c,
  //   99063bca,f6a70,77085ae6,e7b74777,90b077e1,9b9265b,7ebe16cd,e0da836e,97ddb3f8,ed4e242,
  //   79d3d2d4,f4dbdf21,83dcefb7,1ad5be0d,6dd28e9b,f3b61b38,84b12bae,1db87a14,6abf4a82,
  //   fa005713,8d076785,140e363f,630906a9,fd6d930a,8a6aa39c,1363f226,6464c2b0,a4deae1d,
  //   d3d99e8b,4ad0cf31,3dd7ffa7,a3b36a04,d4b45a92,4dbd0b28,3aba3bbe,aa05262f,dd0216b9,
  //   440b4703,330c7795,ad68e236,da6fd2a0,4366831a,3461b38c,b969be79,ce6e8eef,5767df55,
  //   2060efc3,be047a60,c9034af6,500a1b4c,270d2bda,b7b2364b,c0b506dd,59bc5767,2ebb67f1,
  //   b0dff252,c7d8c2c4,5ed1937e,29d6a3e8,9fb08ed5,e8b7be43,71beeff9,6b9df6f,98dd4acc,efda7a5a,
  //   76d32be0,1d41b76,916b06e7,e66c3671,7f6567cb,862575d,9606c2fe,e101f268,7808a3d2,f0f9344,
  //   82079eb1,f500ae27,6c09ff9d,1b0ecf0b,856a5aa8,f26d6a3e,6b643b84,1c630b12,8cdc1683,
  //   fbdb2615,62d277af,15d54739,8bb1d29a,fcb6e20c,65bfb3b6,12b88320,3fba6cad,48bd5c3b,
  //   d1b40d81,a6b33d17,38d7a8b4,4fd09822,d6d9c998,a1def90e,3161e49f,4666d409,df6f85b3,
  //   a868b525,360c2086,410b1010,d80241aa,af05713c,220d7cc9,550a4c5f,cc031de5,bb042d73,
  //   2560b8d0,52678846,cb6ed9fc,bc69e96a,2cd6f4fb,5bd1c46d,c2d895d7,b5dfa541,2bbb30e2,
  //   5cbc0074,c5b551ce,b2b26158,4d44c65,73d37cf3,eada2d49,9ddd1ddf,3b9887c,74beb8ea,edb7e950,
  //   9ab0d9c6,a0fc457,7d08f4c1,e401a57b,930695ed,d62004e,7a6530d8,e36c6162,946b51f4,19635c01,
  //   6e646c97,f76d3d2d,806a0dbb,1e0e9818,6909a88e,f000f934,8707c9a2,17b8d433,60bfe4a5,
  //   f9b6b51f,8eb18589,10d5102a,67d220bc,fedb7106,89dc4190,49662d3d,3e611dab,a7684c11,
  //   d06f7c87,4e0be924,390cd9b2,a0058808,d702b89e,47bda50f,30ba9599,a9b3c423,deb4f4b5,
  //   40d06116,37d75180,aede003a,d9d930ac,54d13d59,23d60dcf,badf5c75,cdd86ce3,53bcf940,
  //   24bbc9d6,bdb2986c,cab5a8fa,5a0ab56b,2d0d85fd,b404d447,c303e4d1,5d677172,2a6041e4,
  //   b369105e,c46e20c8,72080df5,50f3d63,9c066cd9,eb015c4f,7565c9ec,262f97a,9b6ba8c0,ec6c9856,
  //   7cd385c7,bd4b551,92dde4eb,e5dad47d,7bbe41de,cb97148,95b020f2,e2b71064,6fbf1d91,18b82d07,
  //   81b17cbd,f6b64c2b,68d2d988,1fd5e91e,86dcb8a4,f1db8832,616495a3,1663a535,8f6af48f,
  //   f86dc419,660951ba,110e612c,88073096,ff000000
  //   contents of Table_5 (hex, n*v repeats v):
  //   d202ef8d,a505df1b,3c0c8ea1,4b0bbe37,d56f2b94,a2681b02,3b614ab8,4c667a2e,dcd967bf,
  //   abde5729,32d70693,45d03605,dbb4a3a6,acb39330,35bac28a,42bdf21c,cfb5ffe9,b8b2cf7f,
  //   21bb9ec5,56bcae53,c8d83bf0,bfdf0b66,26d65adc,51d16a4a,c16e77db,b669474d,2f6016f7,
  //   58672661,c603b3c2,b1048354,280dd2ee,5f0ae278,e96ccf45,9e6bffd3,762ae69,70659eff,ee010b5c,
  //   99063bca,f6a70,77085ae6,e7b74777,90b077e1,9b9265b,7ebe16cd,e0da836e,97ddb3f8,ed4e242,
  //   79d3d2d4,f4dbdf21,83dcefb7,1ad5be0d,6dd28e9b,f3b61b38,84b12bae,1db87a14,6abf4a82,
  //   fa005713,8d076785,140e363f,630906a9,fd6d930a,8a6aa39c,1363f226,6464c2b0,a4deae1d,
  //   d3d99e8b,4ad0cf31,3dd7ffa7,a3b36a04,d4b45a92,4dbd0b28,3aba3bbe,aa05262f,dd0216b9,
  //   440b4703,330c7795,ad68e236,da6fd2a0,4366831a,3461b38c,b969be79,ce6e8eef,5767df55,
  //   2060efc3,be047a60,c9034af6,500a1b4c,270d2bda,b7b2364b,c0b506dd,59bc5767,2ebb67f1,
  //   b0dff252,c7d8c2c4,5ed1937e,29d6a3e8,9fb08ed5,e8b7be43,71beeff9,6b9df6f,98dd4acc,efda7a5a,
  //   76d32be0,1d41b76,916b06e7,e66c3671,7f6567cb,862575d,9606c2fe,e101f268,7808a3d2,f0f9344,
  //   82079eb1,f500ae27,6c09ff9d,1b0ecf0b,856a5aa8,f26d6a3e,6b643b84,1c630b12,8cdc1683,
  //   fbdb2615,62d277af,15d54739,8bb1d29a,fcb6e20c,65bfb3b6,12b88320,3fba6cad,48bd5c3b,
  //   d1b40d81,a6b33d17,38d7a8b4,4fd09822,d6d9c998,a1def90e,3161e49f,4666d409,df6f85b3,
  //   a868b525,360c2086,410b1010,d80241aa,af05713c,220d7cc9,550a4c5f,cc031de5,bb042d73,
  //   2560b8d0,52678846,cb6ed9fc,bc69e96a,2cd6f4fb,5bd1c46d,c2d895d7,b5dfa541,2bbb30e2,
  //   5cbc0074,c5b551ce,b2b26158,4d44c65,73d37cf3,eada2d49,9ddd1ddf,3b9887c,74beb8ea,edb7e950,
  //   9ab0d9c6,a0fc457,7d08f4c1,e401a57b,930695ed,d62004e,7a6530d8,e36c6162,946b51f4,19635c01,
  //   6e646c97,f76d3d2d,806a0dbb,1e0e9818,6909a88e,f000f934,8707c9a2,17b8d433,60bfe4a5,
  //   f9b6b51f,8eb18589,10d5102a,67d220bc,fedb7106,89dc4190,49662d3d,3e611dab,a7684c11,
  //   d06f7c87,4e0be924,390cd9b2,a0058808,d702b89e,47bda50f,30ba9599,a9b3c423,deb4f4b5,
  //   40d06116,37d75180,aede003a,d9d930ac,54d13d59,23d60dcf,badf5c75,cdd86ce3,53bcf940,
  //   24bbc9d6,bdb2986c,cab5a8fa,5a0ab56b,2d0d85fd,b404d447,c303e4d1,5d677172,2a6041e4,
  //   b369105e,c46e20c8,72080df5,50f3d63,9c066cd9,eb015c4f,7565c9ec,262f97a,9b6ba8c0,ec6c9856,
  //   7cd385c7,bd4b551,92dde4eb,e5dad47d,7bbe41de,cb97148,95b020f2,e2b71064,6fbf1d91,18b82d07,
  //   81b17cbd,f6b64c2b,68d2d988,1fd5e91e,86dcb8a4,f1db8832,616495a3,1663a535,8f6af48f,
  //   f86dc419,660951ba,110e612c,88073096,ff000000
  //   contents of Table_6 (hex, n*v repeats v):
  //   d202ef8d,a505df1b,3c0c8ea1,4b0bbe37,d56f2b94,a2681b02,3b614ab8,4c667a2e,dcd967bf,
  //   abde5729,32d70693,45d03605,dbb4a3a6,acb39330,35bac28a,42bdf21c,cfb5ffe9,b8b2cf7f,
  //   21bb9ec5,56bcae53,c8d83bf0,bfdf0b66,26d65adc,51d16a4a,c16e77db,b669474d,2f6016f7,
  //   58672661,c603b3c2,b1048354,280dd2ee,5f0ae278,e96ccf45,9e6bffd3,762ae69,70659eff,ee010b5c,
  //   99063bca,f6a70,77085ae6,e7b74777,90b077e1,9b9265b,7ebe16cd,e0da836e,97ddb3f8,ed4e242,
  //   79d3d2d4,f4dbdf21,83dcefb7,1ad5be0d,6dd28e9b,f3b61b38,84b12bae,1db87a14,6abf4a82,
  //   fa005713,8d076785,140e363f,630906a9,fd6d930a,8a6aa39c,1363f226,6464c2b0,a4deae1d,
  //   d3d99e8b,4ad0cf31,3dd7ffa7,a3b36a04,d4b45a92,4dbd0b28,3aba3bbe,aa05262f,dd0216b9,
  //   440b4703,330c7795,ad68e236,da6fd2a0,4366831a,3461b38c,b969be79,ce6e8eef,5767df55,
  //   2060efc3,be047a60,c9034af6,500a1b4c,270d2bda,b7b2364b,c0b506dd,59bc5767,2ebb67f1,
  //   b0dff252,c7d8c2c4,5ed1937e,29d6a3e8,9fb08ed5,e8b7be43,71beeff9,6b9df6f,98dd4acc,efda7a5a,
  //   76d32be0,1d41b76,916b06e7,e66c3671,7f6567cb,862575d,9606c2fe,e101f268,7808a3d2,f0f9344,
  //   82079eb1,f500ae27,6c09ff9d,1b0ecf0b,856a5aa8,f26d6a3e,6b643b84,1c630b12,8cdc1683,
  //   fbdb2615,62d277af,15d54739,8bb1d29a,fcb6e20c,65bfb3b6,12b88320,3fba6cad,48bd5c3b,
  //   d1b40d81,a6b33d17,38d7a8b4,4fd09822,d6d9c998,a1def90e,3161e49f,4666d409,df6f85b3,
  //   a868b525,360c2086,410b1010,d80241aa,af05713c,220d7cc9,550a4c5f,cc031de5,bb042d73,
  //   2560b8d0,52678846,cb6ed9fc,bc69e96a,2cd6f4fb,5bd1c46d,c2d895d7,b5dfa541,2bbb30e2,
  //   5cbc0074,c5b551ce,b2b26158,4d44c65,73d37cf3,eada2d49,9ddd1ddf,3b9887c,74beb8ea,edb7e950,
  //   9ab0d9c6,a0fc457,7d08f4c1,e401a57b,930695ed,d62004e,7a6530d8,e36c6162,946b51f4,19635c01,
  //   6e646c97,f76d3d2d,806a0dbb,1e0e9818,6909a88e,f000f934,8707c9a2,17b8d433,60bfe4a5,
  //   f9b6b51f,8eb18589,10d5102a,67d220bc,fedb7106,89dc4190,49662d3d,3e611dab,a7684c11,
  //   d06f7c87,4e0be924,390cd9b2,a0058808,d702b89e,47bda50f,30ba9599,a9b3c423,deb4f4b5,
  //   40d06116,37d75180,aede003a,d9d930ac,54d13d59,23d60dcf,badf5c75,cdd86ce3,53bcf940,
  //   24bbc9d6,bdb2986c,cab5a8fa,5a0ab56b,2d0d85fd,b404d447,c303e4d1,5d677172,2a6041e4,
  //   b369105e,c46e20c8,72080df5,50f3d63,9c066cd9,eb015c4f,7565c9ec,262f97a,9b6ba8c0,ec6c9856,
  //   7cd385c7,bd4b551,92dde4eb,e5dad47d,7bbe41de,cb97148,95b020f2,e2b71064,6fbf1d91,18b82d07,
  //   81b17cbd,f6b64c2b,68d2d988,1fd5e91e,86dcb8a4,f1db8832,616495a3,1663a535,8f6af48f,
  //   f86dc419,660951ba,110e612c,88073096,ff000000
  //   contents of Table_7 (hex, n*v repeats v):
  //   d202ef8d,a505df1b,3c0c8ea1,4b0bbe37,d56f2b94,a2681b02,3b614ab8,4c667a2e,dcd967bf,
  //   abde5729,32d70693,45d03605,dbb4a3a6,acb39330,35bac28a,42bdf21c,cfb5ffe9,b8b2cf7f,
  //   21bb9ec5,56bcae53,c8d83bf0,bfdf0b66,26d65adc,51d16a4a,c16e77db,b669474d,2f6016f7,
  //   58672661,c603b3c2,b1048354,280dd2ee,5f0ae278,e96ccf45,9e6bffd3,762ae69,70659eff,ee010b5c,
  //   99063bca,f6a70,77085ae6,e7b74777,90b077e1,9b9265b,7ebe16cd,e0da836e,97ddb3f8,ed4e242,
  //   79d3d2d4,f4dbdf21,83dcefb7,1ad5be0d,6dd28e9b,f3b61b38,84b12bae,1db87a14,6abf4a82,
  //   fa005713,8d076785,140e363f,630906a9,fd6d930a,8a6aa39c,1363f226,6464c2b0,a4deae1d,
  //   d3d99e8b,4ad0cf31,3dd7ffa7,a3b36a04,d4b45a92,4dbd0b28,3aba3bbe,aa05262f,dd0216b9,
  //   440b4703,330c7795,ad68e236,da6fd2a0,4366831a,3461b38c,b969be79,ce6e8eef,5767df55,
  //   2060efc3,be047a60,c9034af6,500a1b4c,270d2bda,b7b2364b,c0b506dd,59bc5767,2ebb67f1,
  //   b0dff252,c7d8c2c4,5ed1937e,29d6a3e8,9fb08ed5,e8b7be43,71beeff9,6b9df6f,98dd4acc,efda7a5a,
  //   76d32be0,1d41b76,916b06e7,e66c3671,7f6567cb,862575d,9606c2fe,e101f268,7808a3d2,f0f9344,
  //   82079eb1,f500ae27,6c09ff9d,1b0ecf0b,856a5aa8,f26d6a3e,6b643b84,1c630b12,8cdc1683,
  //   fbdb2615,62d277af,15d54739,8bb1d29a,fcb6e20c,65bfb3b6,12b88320,3fba6cad,48bd5c3b,
  //   d1b40d81,a6b33d17,38d7a8b4,4fd09822,d6d9c998,a1def90e,3161e49f,4666d409,df6f85b3,
  //   a868b525,360c2086,410b1010,d80241aa,af05713c,220d7cc9,550a4c5f,cc031de5,bb042d73,
  //   2560b8d0,52678846,cb6ed9fc,bc69e96a,2cd6f4fb,5bd1c46d,c2d895d7,b5dfa541,2bbb30e2,
  //   5cbc0074,c5b551ce,b2b26158,4d44c65,73d37cf3,eada2d49,9ddd1ddf,3b9887c,74beb8ea,edb7e950,
  //   9ab0d9c6,a0fc457,7d08f4c1,e401a57b,930695ed,d62004e,7a6530d8,e36c6162,946b51f4,19635c01,
  //   6e646c97,f76d3d2d,806a0dbb,1e0e9818,6909a88e,f000f934,8707c9a2,17b8d433,60bfe4a5,
  //   f9b6b51f,8eb18589,10d5102a,67d220bc,fedb7106,89dc4190,49662d3d,3e611dab,a7684c11,
  //   d06f7c87,4e0be924,390cd9b2,a0058808,d702b89e,47bda50f,30ba9599,a9b3c423,deb4f4b5,
  //   40d06116,37d75180,aede003a,d9d930ac,54d13d59,23d60dcf,badf5c75,cdd86ce3,53bcf940,
  //   24bbc9d6,bdb2986c,cab5a8fa,5a0ab56b,2d0d85fd,b404d447,c303e4d1,5d677172,2a6041e4,
  //   b369105e,c46e20c8,72080df5,50f3d63,9c066cd9,eb015c4f,7565c9ec,262f97a,9b6ba8c0,ec6c9856,
  //   7cd385c7,bd4b551,92dde4eb,e5dad47d,7bbe41de,cb97148,95b020f2,e2b71064,6fbf1d91,18b82d07,
  //   81b17cbd,f6b64c2b,68d2d988,1fd5e91e,86dcb8a4,f1db8832,616495a3,1663a535,8f6af48f,
  //   f86dc419,660951ba,110e612c,88073096,ff000000
  //   contents of Table_8 (hex, n*v repeats v):
  //   d202ef8d,a505df1b,3c0c8ea1,4b0bbe37,d56f2b94,a2681b02,3b614ab8,4c667a2e,dcd967bf,
  //   abde5729,32d70693,45d03605,dbb4a3a6,acb39330,35bac28a,42bdf21c,cfb5ffe9,b8b2cf7f,
  //   21bb9ec5,56bcae53,c8d83bf0,bfdf0b66,26d65adc,51d16a4a,c16e77db,b669474d,2f6016f7,
  //   58672661,c603b3c2,b1048354,280dd2ee,5f0ae278,e96ccf45,9e6bffd3,762ae69,70659eff,ee010b5c,
  //   99063bca,f6a70,77085ae6,e7b74777,90b077e1,9b9265b,7ebe16cd,e0da836e,97ddb3f8,ed4e242,
  //   79d3d2d4,f4dbdf21,83dcefb7,1ad5be0d,6dd28e9b,f3b61b38,84b12bae,1db87a14,6abf4a82,
  //   fa005713,8d076785,140e363f,630906a9,fd6d930a,8a6aa39c,1363f226,6464c2b0,a4deae1d,
  //   d3d99e8b,4ad0cf31,3dd7ffa7,a3b36a04,d4b45a92,4dbd0b28,3aba3bbe,aa05262f,dd0216b9,
  //   440b4703,330c7795,ad68e236,da6fd2a0,4366831a,3461b38c,b969be79,ce6e8eef,5767df55,
  //   2060efc3,be047a60,c9034af6,500a1b4c,270d2bda,b7b2364b,c0b506dd,59bc5767,2ebb67f1,
  //   b0dff252,c7d8c2c4,5ed1937e,29d6a3e8,9fb08ed5,e8b7be43,71beeff9,6b9df6f,98dd4acc,efda7a5a,
  //   76d32be0,1d41b76,916b06e7,e66c3671,7f6567cb,862575d,9606c2fe,e101f268,7808a3d2,f0f9344,
  //   82079eb1,f500ae27,6c09ff9d,1b0ecf0b,856a5aa8,f26d6a3e,6b643b84,1c630b12,8cdc1683,
  //   fbdb2615,62d277af,15d54739,8bb1d29a,fcb6e20c,65bfb3b6,12b88320,3fba6cad,48bd5c3b,
  //   d1b40d81,a6b33d17,38d7a8b4,4fd09822,d6d9c998,a1def90e,3161e49f,4666d409,df6f85b3,
  //   a868b525,360c2086,410b1010,d80241aa,af05713c,220d7cc9,550a4c5f,cc031de5,bb042d73,
  //   2560b8d0,52678846,cb6ed9fc,bc69e96a,2cd6f4fb,5bd1c46d,c2d895d7,b5dfa541,2bbb30e2,
  //   5cbc0074,c5b551ce,b2b26158,4d44c65,73d37cf3,eada2d49,9ddd1ddf,3b9887c,74beb8ea,edb7e950,
  //   9ab0d9c6,a0fc457,7d08f4c1,e401a57b,930695ed,d62004e,7a6530d8,e36c6162,946b51f4,19635c01,
  //   6e646c97,f76d3d2d,806a0dbb,1e0e9818,6909a88e,f000f934,8707c9a2,17b8d433,60bfe4a5,
  //   f9b6b51f,8eb18589,10d5102a,67d220bc,fedb7106,89dc4190,49662d3d,3e611dab,a7684c11,
  //   d06f7c87,4e0be924,390cd9b2,a0058808,d702b89e,47bda50f,30ba9599,a9b3c423,deb4f4b5,
  //   40d06116,37d75180,aede003a,d9d930ac,54d13d59,23d60dcf,badf5c75,cdd86ce3,53bcf940,
  //   24bbc9d6,bdb2986c,cab5a8fa,5a0ab56b,2d0d85fd,b404d447,c303e4d1,5d677172,2a6041e4,
  //   b369105e,c46e20c8,72080df5,50f3d63,9c066cd9,eb015c4f,7565c9ec,262f97a,9b6ba8c0,ec6c9856,
  //   7cd385c7,bd4b551,92dde4eb,e5dad47d,7bbe41de,cb97148,95b020f2,e2b71064,6fbf1d91,18b82d07,
  //   81b17cbd,f6b64c2b,68d2d988,1fd5e91e,86dcb8a4,f1db8832,616495a3,1663a535,8f6af48f,
  //   f86dc419,660951ba,110e612c,88073096,ff000000
endmodule

/* Test case:
data limit crc
0x68656c6c6f000000 5 0x3610a686
0x756e697465630000 6 0x15c823f8
0x776f726c64000000 5 0x3a771143
0x686f6c61206d756e 8 0xd8c9ff16
*/
