// Digital circuit Microhondas.dig as structural Verilog
module Microhondas (
  input  clk,
  input  clk2,
  output [7:0] out_3
);

  wire _0, _1, _2, _3, _4, _5, _6, _7, _8, _9, c, clean, comparator_1_lt, comparator_2_eq, i,
       multiplexer_1_out, multiplexer_2_out, not_1_out, r10, r11, r12, r13, r14, r15, r16, r17, r20, r21,
       r22, r23, r24, r25, r26, r27, r30, r31, r32, r33, r34, r35, r36, r37, r40, r41, r42, r43, r44, r45,
       r46, r47, start;
  wire [7:0] add_1_s, kpress, mul_1_mul, multiplexer_3_out, multiplexer_4_out, multiplexer_5_out;
  wire [15:8] mul_1_mul_2;

  not not_1 (not_1_out, start);
  Multiplexer multiplexer_1 (.sel(i), .in_0(not_1_out), .in_1(start), .out(multiplexer_1_out));
  Mul #(.Bits(8)) mul_1 (.a(out_3), .b(8'ha), .mul({mul_1_mul_2, mul_1_mul}));
  Multiplexer multiplexer_2 (.sel(multiplexer_1_out), .in_0(1'b1), .in_1(1'b0), .out(multiplexer_2_out));
  Register u_start (.D(multiplexer_2_out), .C(clk), .en(1'b1), .Q(start));
  Add #(.Bits(8)) add_1 (.a(mul_1_mul), .b(kpress), .c_i(1'b0), .s(add_1_s));  // open: c_o
  KeyBoardHandler #(.applicationType("IVERILOG")) u_KeyBoardHandler (
    .a({_9, _8, _7, _6, _5, _4, _3, _2, _1, _0}), .n(kpress));
  Comparator #(.Bits(8)) comparator_1 (.a(out_3), .b(8'ha), .lt(comparator_1_lt));  // open: gt, eq
  Multiplexer #(.Bits(8)) multiplexer_3 (.sel(comparator_1_lt), .in_0(out_3), .in_1(add_1_s), .out(multiplexer_3_out));
  Comparator #(.Bits(8)) comparator_2 (.a(kpress), .b(8'ha), .eq(comparator_2_eq));  // open: gt, lt
  Multiplexer #(.Bits(8)) multiplexer_4 (
    .sel(comparator_2_eq), .in_0(multiplexer_3_out), .in_1(out_3), .out(multiplexer_4_out));
  Multiplexer #(.Bits(8)) multiplexer_5 (.sel(c), .in_0(multiplexer_4_out), .in_1({8{1'b0}}), .out(multiplexer_5_out));
  Button u__0 (.out(_0));
  Button u__3 (.out(_3));
  Button u__6 (.out(_6));
  Register #(.Bits(8)) teclado (.D(multiplexer_5_out), .C(clk2), .en(1'b1), .Q(out_3));
  Button u__1 (.out(_1));
  Button u__4 (.out(_4));
  Button u__7 (.out(_7));
  Button u__9 (.out(_9));
  Button Iniciar___detener (.out(i));
  LED led_1 (.in(start));
  Button Reiniciar (.out(clean));
  Button Limpiar (.out(c));
  Button u__2 (.out(_2));
  Button u__5 (.out(_5));
  Button u__8 (.out(_8));
  Seven_Seg seven_seg_1 (.a(r17), .b(r16), .c(r15), .d(r14), .e(r13), .f(r12), .g(r11), .dp(r10));
  MicroHondas #(.applicationType("IVERILOG")) u_MicroHondas (
    .clk(clk), .rst(clean), .minuto(out_3), .enabled(start), .r1({r17, r16, r15, r14, r13, r12, r11, r10}),
    .r2({r27, r26, r25, r24, r23, r22, r21, r20}), .r3({r37, r36, r35, r34, r33, r32, r31, r30}),
    .r4({r47, r46, r45, r44, r43, r42, r41, r40}));
  Seven_Seg seven_seg_2 (.a(r27), .b(r26), .c(r25), .d(r24), .e(r23), .f(r22), .g(r21), .dp(r20));
  Seven_Seg seven_seg_3 (.a(r37), .b(r36), .c(r35), .d(r34), .e(r33), .f(r32), .g(r31), .dp(r30));
  Seven_Seg seven_seg_4 (.a(r47), .b(r46), .c(r45), .d(r44), .e(r43), .f(r42), .g(r41), .dp(r40));

  // Other names for the same wires on the sheet: r18[7:0] = {r17, r16, r15, r14, r13, r12, r11, r10};
  //   r28[7:0] = {r27, r26, r25, r24, r23, r22, r21, r20}; r38[7:0] = {r37, r36, r35, r34, r33, r32, r31, r30};
  //   r48[7:0] = {r47, r46, r45, r44, r43, r42, r41, r40}; tec[7:0] = out_3

  // Notes on the sheet:
  //   clk: Hz: 2
  //   clk2: Hz: 5
endmodule

/* Code of KeyBoardHandler:
module KeyBoardHandler(
    input [9:0] a,
    output [7:0] n
);
    reg [6:0] nprime;

        assign n = nprime;

    always @(*) begin
        if(a[0]) 
            nprime = 8'd0;
        else if(a[1]) 
            nprime = 8'd1;
        else if(a[2]) 
            nprime = 8'd2;
        else if(a[3]) 
            nprime = 8'd3;
        else if(a[4]) 
            nprime = 8'd4;
        else if(a[5]) 
            nprime = 8'd5;
        else if(a[6]) 
            nprime = 8'd6;
        else if(a[7]) 
            nprime = 8'd7;
        else if(a[8]) 
            nprime = 8'd8;
        else if(a[9]) 
            nprime = 8'd9;
        else
            nprime = 8'd10;

    end

endmodule
*/

/* Code of MicroHondas:
module MicroHondas
(
    input clk,
    input rst,
    input [7:0] minuto,
    input enabled,
    output [7:0] r1,
    output [7:0] r2,
    output [7:0] r3,
    output [7:0] r4
);

    parameter q0 = 3'd0;
    parameter q1 = 3'd1;
    parameter q2 = 3'd2;
    parameter q3 = 3'd3;
    parameter q4 = 3'd4;
    parameter q5 = 3'd5;
    parameter q6 = 3'd6;

    reg [7:0] a, b;
    reg [7:0] snA, snB;

    reg [2:0] cs;
    reg [2:0] ns;

    ConvertToBits cc1(.number(a >8'd0? a- 8'd1 : a), .n1(r1), .n2(r2));
    ConvertToBits cc2(.number(a >8'd0? b : 8'd0), .n1(r3), .n2(r4)); 

always @(*)
begin
   case(cs)

            q0: begin 
                ns = q1;            
            end

            q1: begin
                ns = a!= 8'd0? q2:q6;
            end
            
            q2: begin
                ns = q3;
            end
            
            q3: begin
                ns = b!=8'd0? q2:q4;
            end
            
            q4: begin
                ns = q5;
            end
            
            q5: begin
                ns = a!= 8'd0? q2:q6;
            end
            
            q6: begin
                ns = q6;
            end

            default: begin
                ns = q0; 
            end
        endcase
end

     //Outputs 
    always @(*) begin

        if (enabled) begin
        case(cs)

            q0: begin
                snA = minuto;  
                snB = 8'd60;              
            end

            q1: begin
                snA = a;  
                snB = b; 
            end
            
            q2: begin
                snA = a;  
                snB = b - 8'd1; 
            end
            
            q3: begin
                snA = a;  
                snB = b; 
            end
            
            q4: begin
                snA = a- 8'd1;  
                snB = 60; 
            end
            
            q5: begin
                snA = a;  
                snB = b; 
            end
            
            q6: begin
                snA = a;  
                snB = b; 
            end

            default: begin
                snA = 8'd0;  
                snB = 8'd0; 
            end
        endcase 
        end
    end


    //current state
    always @(posedge clk) begin
        if(rst)
            cs <= q0;
        else 
            cs <= ns;
    end

    always @(posedge clk) begin
        a <= snA;
        b <= snB;
    end

endmodule


module ConvertToBits(
    input [7:0] number,
    output [7:0] n1,
    output [7:0] n2
);

    reg [7:0] contador;
    reg [7:0] comparador;
    reg [7:0] resultBt1;
    reg [7:0] resultBt2;

    Get7ComplementinBits t1(.number(resultBt1), .value(n1));
    Get7ComplementinBits t2(.number(resultBt2), .value(n2));

     always @(*) 
        begin
            comparador = number;
            if (comparador < 10) begin
                resultBt1 = 8'b0;
                resultBt2 = comparador;
            end
            else        
            begin
                contador = 4'b0;
                while(comparador >= 10)
                begin
                    contador = contador + 4'd1;
                    comparador = comparador - 10;
                end
                resultBt1 = contador;
                resultBt2 = comparador;
            end
        end
        

endmodule

//  Modulo para generar digito

module Get7ComplementinBits(
        input [7:0] number,
        output [7:0] value
        );

        reg [7:0] resultBt;
        assign value = resultBt;
        
        always @(*)
        begin
            case (number)
                    0: resultBt <= 8'b11111100;
                    1: resultBt <= 8'b01100000;
                    2: resultBt <= 8'b11011010;
                    3: resultBt <= 8'b11110010;
                    4: resultBt <= 8'b01100110;
                    5: resultBt <= 8'b10110110;
                    6: resultBt <= 8'b00111110;
                    7: resultBt <= 8'b11100000;
                    8: resultBt <= 8'b11111110;
                    9: resultBt <= 8'b11100110;
                    default: resultBt <= 8'b00000000;
                endcase
        end

    endmodule
*/
